// Logisim project ALU.circ as structural Verilog: 1 circuit, main circuit ALU
module ALU (
  input  [31:0] A,
  input  [31:0] B,
  input  [4:0] Shift,
  input  [3:0] Codop,
  input  CarryIn,
  output [31:0] S,
  output [3:0] Flags,
  output CarryOut
);

  wire C_ADC, C_ASR, C_CMN, C_CMP, C_LSL, C_LSR, C_RSB, C_SBC, not_1_out, subtractor_1_bout,
       subtractor_3_bout, V_ADC, V_CMN, V_CMP, V_RSB, V_SBC, xnor_1_out, xnor_2_out, xor_2_out, xor_3_out,
       xor_4_out, xor_5_out, xor_6_out, xor_7_out;
  wire [4:0] subtractor_4_out, subtractor_5_out, subtractor_6_out;
  wire [31:0] ADC, ASR, BIC, CMN, CMP, EOR, ET, LSL, LSR, MUL, multiplexer_2_out, MVN, not_2_out, ORR, R,
       RSB, SBC, TST;

  not not_1 (not_1_out, CarryIn);
  assign not_2_out = ~A;  // NOT_Gate not_2, 32 bits wide
  assign ET = A & B;  // AND_Gate and_1, 32 bits wide
  assign EOR = A ^ B;  // XOR_Gate xor_1, 32 bits wide
  Shifter #(.width(32)) shifter_1 (.in(B), .\dist (Shift), .out(LSL));
  Shifter #(.shift("lr"), .width(32)) shifter_2 (.in(B), .\dist (Shift), .out(LSR));
  Shifter #(.shift("ar"), .width(32)) shifter_3 (.in(B), .\dist (Shift), .out(ASR));
  Adder #(.width(32)) adder_1 (.a(A), .b(B), .out(ADC), .cin(CarryIn), .cout(C_ADC));
  Subtractor #(.width(32)) subtractor_1 (.a(B), .b(A), .out(SBC), .bin(not_1_out), .bout(subtractor_1_bout));
  not not_3 (C_SBC, subtractor_1_bout);
  Shifter #(.shift("rr"), .width(32)) shifter_4 (.in(B), .\dist (Shift), .out(R));
  assign TST = A & B;  // AND_Gate and_2, 32 bits wide
  Subtractor #(.width(32)) subtractor_2 (.a({32{1'b0}}), .b(A), .out(RSB));  // open: bin, bout
  Subtractor #(.width(32)) subtractor_3 (.a(B), .b(A), .out(CMP), .bout(subtractor_3_bout));  // open: bin
  not not_4 (C_CMP, subtractor_3_bout);
  Adder #(.width(32)) adder_2 (.a(A), .b(B), .out(CMN), .cout(C_CMN));  // open: cin
  assign ORR = A | B;  // OR_Gate or_1, 32 bits wide
  Multiplier #(.width(32)) multiplier_1 (.a(A), .b(B), .out(MUL));  // open: cin, cout
  assign BIC = B & not_2_out;  // AND_Gate and_3, 32 bits wide
  assign MVN = ~A;  // NOT_Gate not_5, 32 bits wide
  BitSelector #(.width(32)) bitselector_1 (.in(B), .out(C_LSL), .sel(subtractor_4_out));
  Subtractor #(.width(5)) subtractor_4 (.a({5{1'b0}}), .b(Shift), .out(subtractor_4_out));  // open: bin, bout
  BitSelector #(.width(32)) bitselector_2 (.in(B), .out(C_LSR), .sel(subtractor_5_out));
  Subtractor #(.width(5)) subtractor_5 (.a(Shift), .b(5'b00001), .out(subtractor_5_out));  // open: bin, bout
  BitSelector #(.width(32)) bitselector_3 (.in(B), .out(C_ASR), .sel(subtractor_6_out));
  Subtractor #(.width(5)) subtractor_6 (.a(Shift), .b(5'b00001), .out(subtractor_6_out));  // open: bin, bout
  BitSelector #(.width(32)) bitselector_4 (.in(R), .out(C_LSR), .sel({5{1'b1}}));
  Comparator #(.width(32)) comparator_1 (.a(A), .b(32'h4c4b400), .eq(C_RSB));  // open: gt, lt
  xnor xnor_1 (xnor_1_out, A[31], B[31]);
  xor xor_2 (xor_2_out, A[31], ADC[31]);
  xor xor_3 (xor_3_out, A[31], B[31]);
  xor xor_4 (xor_4_out, B[31], SBC[31]);
  xor xor_5 (xor_5_out, A[31], B[31]);
  xor xor_6 (xor_6_out, B[31], CMP[31]);
  xnor xnor_2 (xnor_2_out, A[31], B[31]);
  xor xor_7 (xor_7_out, A[31], CMN[31]);
  and and_4 (V_ADC, xnor_1_out, xor_2_out);
  and and_5 (V_CMP, xor_5_out, xor_6_out);
  and and_6 (V_CMN, xnor_2_out, xor_7_out);
  and and_7 (V_SBC, xor_3_out, xor_4_out);
  Comparator #(.width(32)) comparator_2 (.a(A), .b(32'h4c4b400), .eq(V_RSB));  // open: gt, lt
  Multiplexer #(.select(4), .width(32)) multiplexer_1 (
    .in0(ET), .in1(EOR), .in2(LSL), .in3(LSR), .in4(ASR), .in5(ADC), .in6(SBC), .in7(R), .in8(B), .in9(RSB),
    .in10(B), .in11(B), .in12(ORR), .in13(MUL), .in14(BIC), .in15(MVN), .out(S), .sel(Codop));
  Multiplexer #(.select(4), .width(32)) multiplexer_2 (
    .in0(S), .in1(S), .in2(S), .in3(S), .in4(S), .in5(S), .in6(S), .in7(S), .in8(TST), .in9(S), .in10(CMP),
    .in11(CMN), .in12(S), .in13(S), .in14(S), .in15(S), .out(multiplexer_2_out), .sel(Codop));
  Multiplexer #(.select(4)) multiplexer_3 (
    .in0(1'b0), .in1(1'b0), .in2(C_LSL), .in3(C_LSR), .in4(C_ASR), .in5(C_ADC), .in6(C_SBC), .in7(C_LSR),
    .in8(1'b0), .in9(C_RSB), .in10(C_CMP), .in11(C_CMN), .in12(1'b0), .in13(1'b0), .in14(1'b0), .in15(1'b0),
    .out(CarryOut), .sel(Codop));
  Multiplexer #(.select(4)) multiplexer_4 (
    .in0(1'b0), .in1(1'b0), .in2(1'b0), .in3(1'b0), .in4(1'b0), .in5(V_ADC), .in6(V_SBC), .in7(1'b0),
    .in8(1'b0), .in9(V_RSB), .in10(V_CMP), .in11(V_CMN), .in12(1'b0), .in13(1'b0), .in14(1'b0), .in15(1'b0),
    .out(Flags[0]), .sel(Codop));
  Comparator #(.width(32)) comparator_3 (
    .a(multiplexer_2_out), .b({32{1'b0}}), .eq(Flags[2]), .lt(Flags[3]));  // open: gt

  assign Flags[1] = CarryOut;

  // Other names for the same wires on the sheet: A_SIGN_BIT = A[31]; CIn = CarryIn; Co[3:0] = Codop; V = Flags[0];
  //   C = CarryOut; Z = Flags[2]; N = Flags[3]; MAIN_OUTPUT[31:0] = S; O_CMN[31:0] = B; O_CMP[31:0] = B;
  //   O_TST[31:0] = B; B_SIGN_BIT = B[31]; S_t[4:0] = Shift

  // Notes on the sheet:
  //   Note: for ROR, C = N
  //   Note 2: assume that shift > 0 for LSL and LSR
endmodule
