// Logisim project BancDeRegistres.circ as structural Verilog: 1 circuit, main circuit BancRegistre
module BancRegistre (
  input  [31:0] DataIn,
  input  [2:0] RegA,
  input  [2:0] RegB,
  input  [2:0] RegDest,
  input  Clk,
  input  Reset,
  output [31:0] AOut,
  output [31:0] BOut,
  output [31:0] R0,
  output [31:0] R1,
  output [31:0] R2,
  output [31:0] R3,
  output [31:0] R4,
  output [31:0] R5,
  output [31:0] R6,
  output [31:0] R7
);

  wire decoder_1_out0, decoder_1_out1, decoder_1_out2, decoder_1_out3, decoder_1_out4, decoder_1_out5,
       decoder_1_out6, decoder_1_out7, NO_CLK, RegA_0_OUT, RegA_1_OUT;

  Decoder #(.select(3)) decoder_1 (
    .out0(decoder_1_out0), .out1(decoder_1_out1), .out2(decoder_1_out2), .out3(decoder_1_out3),
    .out4(decoder_1_out4), .out5(decoder_1_out5), .out6(decoder_1_out6), .out7(decoder_1_out7),
    .sel(RegDest), .en(1'b1));
  not not_1 (NO_CLK, Clk);
  Register #(.width(32)) register_1 (.D(DataIn), .en(decoder_1_out1), .clk(Clk), .Q(R1), .clr(Reset));
  Register #(.width(32)) register_2 (.D(DataIn), .en(decoder_1_out3), .clk(Clk), .Q(R3), .clr(Reset));
  Register #(.width(32)) register_3 (.D(DataIn), .en(decoder_1_out5), .clk(Clk), .Q(R5), .clr(Reset));
  Register #(.width(32)) register_4 (.D(DataIn), .en(decoder_1_out7), .clk(Clk), .Q(R7), .clr(Reset));
  Register #(.width(32)) register_5 (.D(DataIn), .en(decoder_1_out0), .clk(Clk), .Q(R0), .clr(Reset));
  Register #(.width(32)) register_6 (.D(DataIn), .en(decoder_1_out2), .clk(Clk), .Q(R2), .clr(Reset));
  Register #(.width(32)) register_7 (.D(DataIn), .en(decoder_1_out4), .clk(Clk), .Q(R4), .clr(Reset));
  Register #(.width(32)) register_8 (.D(DataIn), .en(decoder_1_out6), .clk(Clk), .Q(R6), .clr(Reset));
  Decoder #(.select(3)) decoder_2 (
    .out0(RegA_0_OUT), .out1(RegA_1_OUT), .sel(RegA), .en(1'b1));  // open: out2, out3, out4, out5, out6, out7
  Register #(.width(32)) register_9 (.D(R0), .en(RegA_0_OUT), .clk(NO_CLK));  // open: Q, clr
  Register #(.width(32)) register_10 (.D(R1), .en(RegA_1_OUT), .clk(NO_CLK));  // open: Q, clr

  // Other names for the same wires on the sheet: R0_DATA[31:0] = R0; R1_DATA[31:0] = R1; RegA_Entry[2:0] = RegA;
  //   RegA_OUT[31:0] = AOut; RegB_Entry[2:0] = RegB; RegB_OUT[31:0] = BOut
endmodule
