// Logisim project Ctl_Conditional.circ as structural Verilog: 1 circuit, main circuit Conditional
module Conditional (
  input  Enable,
  input  [15:0] Instruction,
  input  Z,
  input  C,
  input  N,
  input  V,
  output [10:0] Offset,
  output Verified
);

  wire CC_LO, GE, GT, HI, LE, LS, LT, MUX_OUT, NE, not_5_out, not_6_out, not_7_out, PL, undriven, VC,
       xnor_2_out, xor_2_out;
  wire [3:0] CODE_COND;
  wire [7:0] IMM8;
  wire [10:0] IMM11;

  not not_1 (NE, Z);
  not not_2 (CC_LO, C);
  not not_3 (PL, N);
  not not_4 (VC, V);
  not not_5 (not_5_out, Z);
  not not_6 (not_6_out, C);
  not not_7 (not_7_out, Z);
  and and_1 (HI, C, not_5_out);
  or or_1 (LS, not_6_out, Z);
  xnor xnor_1 (GE, V, N);
  xor xor_1 (LT, V, N);
  xnor xnor_2 (xnor_2_out, V, N);
  xor xor_2 (xor_2_out, V, N);
  BitSelector #(.group(11), .width(16)) bitselector_1 (.in(Instruction), .out(IMM11), .sel(undriven));
  BitSelector #(.group(8), .width(16)) bitselector_2 (.in(Instruction), .out(IMM8), .sel(1'b0));
  BitSelector #(.group(4), .width(16)) bitselector_3 (.in(Instruction), .out(CODE_COND), .sel(2'b10));
  and and_2 (GT, not_7_out, xnor_2_out);
  and and_3 (LE, Z, xor_2_out);
  Multiplexer #(.enable("false"), .select(4)) multiplexer_1 (
    .in0(Z), .in1(NE), .in2(C), .in3(CC_LO), .in4(N), .in5(PL), .in6(V), .in7(VC), .in8(HI), .in9(LS),
    .in10(GE), .in11(LT), .in12(GT), .in13(LE), .in14(1'b1), .in15(1'b1), .out(MUX_OUT), .sel(CODE_COND));

  // Other names for the same wires on the sheet: CS_HS = C; FLAG_C = C; EQ = Z; FLAG_Z = Z; FLAG_N = N; MI = N;
  //   FLAG_V = V; VS = V
endmodule
