// Logisim project Ctl_Data_Processing.circ as structural Verilog: 2 circuits, main circuit Data_Processing
module Data_Processing (
  input  Enable,
  input  [15:0] Instruction,
  output [2:0] Rd,
  output [2:0] Rn,
  output [2:0] Rm,
  output [3:0] ALU_Opcode,
  output [3:0] Flags_Update_Mask
);

  wire [2:0] spec_entry_1_out_n;

  Demultiplexer #(.select(3), .width(6)) demultiplexer_1 (
    .out0({Rd, Rd}), .out1({Rd, Rd}), .out2({Rd, Rd}), .out3({Rd, Rd}), .out4({Rd, Rd}),
    .in(Instruction[5:0]), .sel(spec_entry_1_out_n));  // open: out5, out6, out7
  spec_entry spec_entry_1 (.OPCODE_IN(Instruction[9:6]), .OUT_N(spec_entry_1_out_n));

  assign ALU_Opcode = Instruction[9:6];
  assign Rm = Rd;
  assign Rn = Rd;

  // Other names for the same wires on the sheet: RD_OUT[2:0] = Rd; RM_OUT[2:0] = Rd; RN_OUT[2:0] = Rd;
  //   Rndm[5:0] = Instruction[5:0]; OPCODE_OUT[3:0] = Instruction[9:6]

  // Notes on the sheet:
  //   Note 2: RSB instruction has Rn as 1st operand.
  //   MUL instruction has Rn as 1st operand and Rdm as 2nd operand
  //   For simplification purposes, Rm is used for 1st operand both here and in the ALU.
  //   Note: instructions that does not save the result will still have the second operand as the destination register, the ALU will copy the second register to the destination register
  //   Pull output low on Enable = 0
endmodule

module spec_entry (
  input  [3:0] OPCODE_IN,
  output [2:0] OUT_N
);

  wire and_3_out, and_4_out, and_5_out, not_1_out, not_2_out, not_3_out;

  not not_1 (not_1_out, OPCODE_IN[2]);
  not not_2 (not_2_out, OPCODE_IN[1]);
  not not_3 (not_3_out, OPCODE_IN[0]);
  and and_1 (OUT_N[2], OPCODE_IN[3], OPCODE_IN[2], OPCODE_IN[1], OPCODE_IN[0]);
  and and_2 (OUT_N[1], OPCODE_IN[3], not_2_out, OPCODE_IN[0]);
  and and_3 (and_3_out, OPCODE_IN[3], not_1_out, not_3_out);
  and and_4 (and_4_out, OPCODE_IN[3], not_1_out, OPCODE_IN[1]);
  or or_1 (OUT_N[0], and_3_out, and_4_out, and_5_out);
  and and_5 (and_5_out, OPCODE_IN[3], OPCODE_IN[2], not_2_out, OPCODE_IN[0]);
endmodule
