// Logisim project Ctl_Opcode_Decoder.circ as structural Verilog: 2 circuits, main circuit Opcode_Decoder
module Opcode_Decoder (
  input  [5:0] Opcode,
  output Shift,
  output Data_Processing,
  output Load_Store,
  output SP_Address,
  output Conditional
);

  SC_OPCODERDECODER sc_opcoderdecoder_1 (
    .Opcode(Opcode), .Shift(Shift), .Data_Processing(Data_Processing), .Load_Store(Load_Store),
    .SP_Address(SP_Address), .Conditional(Conditional));

  // Notes on the sheet:
  //   Shift, add, sub, mov
  //   Load/Store
  //   SP Address
  //   Data Processing
  //   Conditional branch
endmodule

module SC_OPCODERDECODER (
  input  [5:0] Opcode,
  output Shift,
  output Data_Processing,
  output Load_Store,
  output SP_Address,
  output Conditional
);

  wire and_5_out, and_6_out, not_1_out, not_2_out, not_3_out, not_4_out;

  not not_1 (not_1_out, Opcode[5]);
  not not_2 (not_2_out, Opcode[4]);
  not not_3 (not_3_out, Opcode[3]);
  not not_4 (not_4_out, Opcode[2]);
  and and_1 (Shift, not_1_out, not_2_out);
  and and_2 (Data_Processing, not_1_out, Opcode[4]);
  and and_3 (Load_Store, Opcode[5], not_2_out, not_3_out, Opcode[2]);
  and and_4 (SP_Address, Opcode[5], not_2_out, Opcode[3], Opcode[2]);
  and and_5 (and_5_out, Opcode[5], Opcode[4], not_3_out, Opcode[2]);
  and and_6 (and_6_out, Opcode[5], Opcode[4], Opcode[3], not_4_out);
  or or_1 (Conditional, and_5_out, and_6_out);
endmodule
