// Logisim project Ctl_SP_Address.circ as structural Verilog: 1 circuit, main circuit SP_Address
module SP_Address (
  input  [31:0] Stack_Pointer,
  input  [15:0] Instruction,
  input  Enable,
  output [31:0] New_Stack_Pointer,
  output Write_Enable
);

  wire [31:0] ADD, bit_extender_1_out, bit_extender_2_out, SP, sub;

  assign bit_extender_1_out = {{24{Instruction[7]}}, Instruction[7:0]};  // Bit_Extender bit_extender_1
  assign bit_extender_2_out = {{24{Instruction[7]}}, Instruction[7:0]};  // Bit_Extender bit_extender_2
  Adder #(.width(32)) adder_1 (.a(SP), .out(ADD));  // open: b, cin, cout
  Subtractor #(.width(32)) subtractor_1 (.a(SP), .b(bit_extender_2_out), .out(sub));  // open: bin, bout
  Multiplexer #(.enable("false"), .width(32)) multiplexer_1 (
    .in0(ADD), .in1(sub), .out(New_Stack_Pointer), .sel(Instruction[8]));

  assign Write_Enable = Enable;

  // Other names for the same wires on the sheet: IMM7[7:0] = Instruction[7:0]; Instructions[15:0] = Instruction;
  //   ADD_SUB_ORDER = Instruction[8]; MUX_out[31:0] = New_Stack_Pointer

  // Notes on the sheet:
  //   Pull output low on Enable = 0
endmodule
